# Fritzing sketch RF-RFID_System_final (saved by Fritzing 1.0.5)
perfboards: 3

parts:
  Parça1 = Arduino Nano (Rev3.0) (ICSP)
  A1 = Hiletgo 315mhz rx [package=THT]
  A2 = Hiletgo 315mhz tx [package=THT]
  S1 = Momentary Switch [package=ksa_sealed_tac_switch]
  S2 = Momentary Switch [package=ksa_sealed_tac_switch]
  S3 = Momentary Switch [package=ksa_sealed_tac_switch]
  R1 = Resistor [tolerance=±5% resistance=220 power=0.25W package=THT]
  R2 = Resistor [tolerance=±5% resistance=220 power=0.25W package=THT]
  R3 = Resistor [tolerance=±5% resistance=220 power=0.25W package=THT]
  Parça2 = Arduino Nano (Rev3.0) (ICSP)
  M2 = Dagu DGServo 9g (Top view) [part_number=RS001B]
  M3 = Dagu DGServo 9g (Top view) [part_number=RS001B]
  BAT1 = BC9VPC [package=bc9vpc]
  BAT2 = BC9VPC [package=bc9vpc]
  125_kHz_RFID_module1 = RDM6300
  Parça3 = RDM6300-ANT  # not connected
  R4 = Resistor [tolerance=±5% resistance=220 power=0.25W package=THT]
  R5 = Resistor [tolerance=±5% resistance=220 power=0.25W package=THT]
  LED3 = LED - 5mm [color="Red (633nm)" current=0.030A package="5 mm [THT]"]
  LED4 = LED - 5mm [color="Green (555nm)" current=0.030A package="5 mm [THT]"]

nets:
  N1: Parça1.GND, A2.pin3, R1.Pin_1, BAT1.V-
  N2: Parça1.D2, S1.3, R3.Pin_0
  N3: Parça1.D3, S2.3, R2.Pin_0
  N4: Parça1.D4, S3.3, R1.Pin_0
  N5: Parça1.D5, A2.pin2
  N6: Parça1.VIN, BAT1.V+
  N7: Parça1.5V, A2.pin1, S3.2
  N8: A1.pin1, M3.vcc
  N9: A1.pin2, A1.pin3, Parça2.D11/MOSI
  GND: Parça2.GND, M2.gnd, BAT2.V-
  N10: Parça2.D3, 125_kHz_RFID_module1.RX
  N11: Parça2.D4, 125_kHz_RFID_module1.TX, 125_kHz_RFID_module1.GND#67
  N12: Parça2.D5, R5.Pin_1
  N13: Parça2.D7, R4.Pin_1
  N14: Parça2.D9, M3.pulse
  N15: Parça2.D10, M2.pulse
  N16: Parça2.VIN, BAT2.V+
  5V: Parça2.5V, M2.vcc
  N17: R4.Pin_0, LED4.cathode
  N18: R5.Pin_0, LED3.cathode

notes:
  RF Transmitter
  RF / RFID Receiver

custom parts:
  Hiletgo 315mhz rx: 315Mhz RF Transmitter and Receiver Module link kit, receiver.
  Hiletgo 315mhz tx: 315Mhz RF Transmitter and Receiver Module link kit, transmitter.
  RDM6300: 125 kHz RFID module (serial interface)
  RDM6300-ANT: Antenna
